# Fritzing sketch Tmer_Keeper_Schematic_Diagram (saved by Fritzing 0.9.3b)
breadboards: 1

parts:
  Part1 = LCD1602-I2C
  Part2 = Arduino Uno (Rev3) - ICSP
  UP = Pushbutton [package="[SMD]"]
  DOWN = Pushbutton [package="[THT]"]
  RIGHT = Momentary Switch [package=ksa_sealed_tac_switch]
  LEFT = Momentary Switch [package=ksa_sealed_tac_switch]
  Menu = Pushbutton [package="[THT]"]
  ZS-042_RTC1 = ZS-042 RTC Module
  R1 = Resistor [tolerance=±5% resistance=10k package=THT]
  R2 = Resistor [tolerance=±5% resistance=10k package=THT]
  R3 = Resistor [tolerance=±5% resistance=10k package=THT]
  R4 = Resistor [tolerance=±5% resistance=220 package=THT]
  R5 = Resistor [tolerance=±5% resistance=10k package=THT]
  R6 = Resistor [tolerance=±5% resistance=10k package=THT]
  Buzzer = Piezo Speaker

nets:
  GND: Part1.GND, Part2.GND, ZS-042_RTC1.GND, R1.Pin_1, R2.Pin_1, R3.Pin_1, R4.Pin_1, R5.Pin_1, Buzzer.pin1
  VCC: Part1.VCC, Part2.5V, UP.Pin_1, UP.Pin_2, DOWN.Pin_1, DOWN.Pin_2, RIGHT.1, LEFT.1, Menu.Pin_1, Menu.Pin_2, ZS-042_RTC1.VCC
  N1: Part1.SDA, Part2.A4/SDA, ZS-042_RTC1.SDA
  N2: Part1.SCL, Part2.A5/SCL, ZS-042_RTC1.SCL
  N3: Part2.D2, LEFT.3
  N4: Part2.D3_PWM, UP.Pin_3, UP.Pin_4, R1.Pin_0
  N5: Part2.D4, RIGHT.3
  N6: Part2.D5_PWM, DOWN.Pin_3, DOWN.Pin_4, R2.Pin_0
  N7: Part2.D6_PWM, Menu.Pin_3, Menu.Pin_4, R5.Pin_0
  N8: Part2.D7, R6.Pin_1
  N9: RIGHT.4, R4.Pin_0
  N10: LEFT.4, R3.Pin_0
  N11: R6.Pin_0, Buzzer.pin2

notes:
  I2C 2X16 LCD
  RTC module
  Arduino Uno

custom parts:
  LCD1602-I2C: A standard character display, usually with 2x16 characters. Comes in many colors with LCM1602 IIC attached.
